# Fritzing sketch Motor (saved by Fritzing 0.9.3b)
circuit board: 18.5cm x 9.27648cm
breadboards: 1

parts:
  U3 = atmega328 [package=dip]
  D4 = Resistor [tolerance=±5% resistance=220 part_number=D_4148 package=THT]
  +_- = LED - 5mm [color="Red (633nm)" package="5 mm [THT]"]
  D1 = Resistor [tolerance=±5% resistance=4.7k part_number=Diode_5822_3A package=THT]
  R21 = Resistor [tolerance=±5% resistance=1k package=THT]
  R17 = Resistor [tolerance=±5% resistance=10k package=THT]
  J58 = rounded female pin header, 3 pins [form="♀ (female rounded)"]
  XTAL = Crystal [frequency="16 Mhz" package=THT]
  R2 = Resistor [tolerance=±5% resistance=100 package=THT]
  Q5 = NPN-Transistor [part_number=2N2222A package="TO92 [THT]"]
  R15 = Resistor [tolerance=±5% resistance=1k package=THT]
  Q2 = NPN-Transistor [package="TO92 [THT]"]
  C6 = Ceramic Capacitor [capacitance=22pF package="100 mil [THT, multilayer]"]
  C5 = Ceramic Capacitor [capacitance=22pF package="100 mil [THT, multilayer]"]
  RL1 = OMRON PCB Power Relay – G5LE [part_number="G5LE-1\n" package=THT]
  D5 = Resistor [tolerance=±5% resistance=220 part_number=D_4148 package=THT]
  Q6 = NPN-Transistor [part_number=2N2222A package="TO92 [THT]"]
  R19 = Resistor [tolerance=±5% resistance=1k package=THT]
  R20 = Resistor [tolerance=±5% resistance=1k package=THT]
  +_-_2 = LED - 5mm [color="Red (633nm)" package="5 mm [THT]"]
  - = screw terminal, 2 pins
  C1 = Resistor [tolerance=±5% resistance=220 part_number="0.47uF Cap" package=THT]
  C7 = Ceramic Capacitor [capacitance="100 nF" package="100 mil [THT, multilayer]"]
  C3 = Ceramic Capacitor [capacitance="100 nF" package="100 mil [THT, multilayer]"]
  C10 = Electrolytic Capacitor [capacitance=33µF voltage=25V package="100 mil [THT, electrolytic]"]
  RL2 = OMRON PCB Power Relay – G5LE [part_number="G5LE-1\n" package=THT]
  C11 = Electrolytic Capacitor [capacitance=33µF voltage=25V package="100 mil [THT, electrolytic]"]
  R13 = Resistor [tolerance=±5% resistance=1k package=THT]
  R14 = Resistor [tolerance=±5% resistance=1k package=THT]
  R16 = Resistor [tolerance=±5% resistance=1k package=THT]
  C9 = Ceramic Capacitor [capacitance="100 nF" package="100 mil [THT, multilayer]"]
  C8 = Ceramic Capacitor [capacitance="100 nF" package="100 mil [THT, multilayer]"]
  Q10 = MOSFET-NCHANNEL [package=sot23-3]
  Q4 = Sharp PC817 [package=THT]
  R12 = Resistor [tolerance=±5% resistance=1k package=THT]
  R_Y = screw terminal, 2 pins
  C2 = Capacitor Polarized [package=cpol-radial-1000uf-25v]
  R11 = Resistor [tolerance=±5% resistance=1k package=THT]
  R22 = Resistor [tolerance=±5% resistance=56k package=THT]
  R23 = Resistor [tolerance=±5% resistance=56k package=THT]
  R25 = Resistor [tolerance=±5% resistance=56k package=THT]
  R27 = Resistor [tolerance=±5% resistance=56k package=THT]
  R29 = Resistor [tolerance=±5% resistance=56k package=THT]
  R24 = Resistor [tolerance=±5% resistance=56k package=THT]
  R26 = Resistor [tolerance=±5% resistance=22k package=THT]
  R28 = Resistor [tolerance=±5% resistance=22k package=THT]
  M1 = V18ZA2P [package=v18za2p]
  M2 = V18ZA2P [package=v18za2p]
  D6 = Diode [package=diode-1n4001]
  D7 = Diode [package=diode-1n4001]
  C_START_STOP = screw terminal, 3 pins
  SIM800L_20MM1 = SIM800L_20MM
  B_Y_R = screw terminal, 3 pins
  Q3 = Sharp PC817 [package=THT]
  Q7 = Sharp PC817 [package=THT]
  Q8 = Sharp PC817 [package=THT]
  Q9 = Sharp PC817 [package=THT]
  J48 = rounded female pin header, 2 pins [form="♀ (female rounded)"]
  RESET1 = Pushbutton [package="[THT]"]
  ON/OFF = SWITCH-DPDT [package=os]
  J60 = Rectifier_6A [package=THT]
  J69 = 3pth XH JST Custom [form="♀ (female rounded)" package=THT]
  J72 = 4pth XH JST CUSTOM [form="♀ (female rounded)" package=THT]
  J73 = 4pth XH JST CUSTOM [form="♀ (female rounded)" package=THT]
  J77 = 2PTH JST FROM HEADER 5 [form="♀ (female rounded)" package=THT]
  C12 = Electrolytic Capacitor [capacitance=0.47mF voltage=10V package="200 mil [THT, electrolytic]"]

nets:
  N1: U3.RESET, R17.Pin_1, RESET1.Pin_1, RESET1.Pin_2
  N2: U3.D0_(RX), J48.pin1
  N3: U3.D1_(TX), J48.pin2
  N4: U3.D2, R16.Pin_0
  N5: U3.D3_(PWM), R15.Pin_1
  N6: U3.VCC, U3.AVCC, U3.AREF, D4.Pin_0, R17.Pin_0, RL1.COIL2, D5.Pin_1, R19.Pin_1, C7.1, C3.1, RL2.COIL1, C9.0, C8.1, Q10.D, Q4.Pin_4, SIM800L_20MM1.PIN2, Q3.Pin_4, C12.+
  N7: U3.GND, Q5.E, Q2.E, C6.0, C5.1, Q6.E, C7.0, C10.-, C11.-, C9.1, C8.0, SIM800L_20MM1.PIN_6, Q7.Pin_3, Q8.Pin_3, Q9.Pin_3, RESET1.Pin_3, RESET1.Pin_4, C12.-
  N8: U3.XLAT1, XTAL.pin_0, C5.0
  N9: U3.XLAT2, XTAL.pin_1, C6.1
  N10: U3.D5_(PWM), J58.pin1
  N11: U3.D6_(PWM), J58.pin2
  N12: U3.D7, J58.pin3
  N13: U3.D9_(PWM), R14.Pin_0
  N14: U3.D10_(PWM), R13.Pin_0
  N15: U3.D11_(PWM), R12.Pin_1
  N16: U3.A4, +_-.cathode
  N17: U3.A5, +_-_2.cathode
  N18: D4.Pin_1, Q5.C, RL1.COIL1
  N19: +_-.anode, Q4.Pin_2
  N20: D1.Pin_0, C2.+, J60.DC_+
  N21: D1.Pin_1, R2.Pin_0, C1.Pin_0, Q10.G, R11.Pin_1
  N22: R21.Pin_0, Q5.B
  N23: R21.Pin_1, Q4.Pin_3
  N24: R2.Pin_1, C1.Pin_1, C3.0, Q9.Pin_2, ON/OFF.3, ON/OFF.6
  N25: R15.Pin_0, Q2.B
  N26: Q2.C, SIM800L_20MM1.PIN_8
  N27: RL1.A, C_START_STOP.pin2
  N28: RL1.C, RL2.C, C_START_STOP.pin1
  N29: D5.Pin_0, Q6.C, RL2.COIL2
  N30: Q6.B, R20.Pin_1
  N31: R19.Pin_0, Q4.Pin_1, Q3.Pin_1
  N32: R20.Pin_0, Q3.Pin_3
  N33: +_-_2.anode, Q3.Pin_2
  N34: -.pin1, C2.-, ON/OFF.2, ON/OFF.5, J60.DC_-
  N35: -.pin2, Q10.S
  N36: C10.+, R14.Pin_1, Q7.Pin_4
  N37: RL2.B, C_START_STOP.pin3
  N38: C11.+, R13.Pin_1, Q8.Pin_4
  N39: R16.Pin_1, SIM800L_20MM1.PIN_7
  N40: R12.Pin_0, Q9.Pin_4
  N41: R_Y.pin1, J69.pin3
  N42: R_Y.pin2, J69.pin1
  N43: R11.Pin_0, Q9.Pin_1
  N44: R22.Pin_0, R25.Pin_0, B_Y_R.pin1
  N45: R22.Pin_1, M1.P$2, D6.C
  N46: R23.Pin_0, B_Y_R.pin2
  N47: R23.Pin_1, R27.Pin_0, M1.P$1
  N48: R25.Pin_1, R29.Pin_0, M2.P$1
  N49: R27.Pin_1, J72.pin3
  N50: R29.Pin_1, J72.pin1
  N51: R24.Pin_0, B_Y_R.pin3
  N52: R24.Pin_1, M2.P$2, D7.C
  N53: R26.Pin_0, J72.pin4
  N54: R26.Pin_1, D6.A
  N55: R28.Pin_0, J72.pin2
  N56: R28.Pin_1, D7.A
  N57: Q7.Pin_1, J73.pin3
  N58: Q7.Pin_2, J73.pin4
  N59: Q8.Pin_1, J73.pin1
  N60: Q8.Pin_2, J73.pin2
  N61: J60.AC_IN#1, J77.pin1
  N62: J60.AC_IN#2, J77.pin2

notes:
  M-
  RX
  TX
  STX
  SRX
  1
  C
  MOTOR
  l
  FeedBack
  +
  Battery
  J1
  J2
  Krishna
  M Commander

custom parts:
  Rectifier_6A: stand Up rectifier 6A
  3pth XH JST Custom: 3PTH XH JST
  2PTH JST FROM HEADER 5: Generic rounded female header
