# Fritzing sketch Motor Test Sketch (saved by Fritzing 0.9.3b)
circuit board: 18.5cm x 8.63842cm
breadboards: 1

parts:
  R17 = Resistor [tolerance=±5% resistance=10k package=THT]
  XTAL = Crystal [frequency="16 Mhz" package=THT]
  R15 = Resistor [tolerance=±5% resistance=1k package=THT]
  Q2 = NPN-Transistor [part_number=2N2222A package="TO92 [THT]"]
  C6 = Ceramic Capacitor [capacitance=22pF package="100 mil [THT, multilayer]"]
  C5 = Ceramic Capacitor [capacitance=22pF package="100 mil [THT, multilayer]"]
  - = screw terminal, 2 pins
  C7 = Ceramic Capacitor [capacitance="100 nF" package="100 mil [THT, multilayer]"]
  C10 = Electrolytic Capacitor [capacitance=33µF voltage=25V package="100 mil [THT, electrolytic]"]
  R14 = Resistor [tolerance=±5% resistance=1k package=THT]
  R16 = Resistor [tolerance=±5% resistance=1k package=THT]
  C9 = Ceramic Capacitor [capacitance="100 nF" package="100 mil [THT, multilayer]"]
  C8 = Ceramic Capacitor [capacitance="100 nF" package="100 mil [THT, multilayer]"]
  Q10 = MOSFET-NCHANNEL [package=sot23-3]
  R25 = Resistor [tolerance=±5% resistance=56k package=THT]
  R29 = Resistor [tolerance=±5% resistance=22k package=THT]
  R24 = Resistor [tolerance=±5% resistance=56k package=THT]
  R28 = Resistor [tolerance=±5% resistance=22k package=THT]
  SIM800L_20MM1 = SIM800L_20MM
  J48 = rounded female pin header, 2 pins [form="♀ (female rounded)"]
  RESET1 = Pushbutton [package="[THT]"]
  J77 = 2PTH JST FROM HEADER 5 [form="♀ (female rounded)" package=THT]
  C12 = Electrolytic Capacitor [capacitance=0.47mF voltage=10V package="200 mil [THT, electrolytic]"]
  R30 = Resistor [tolerance=±5% resistance=1k package=THT]
  C2 = Capacitor Polarized [package=cpol-radial-1000uf-25v]
  R32 = Resistor [tolerance=±5% resistance=1k package=THT]
  R33 = Resistor [tolerance=±5% resistance=2k package=THT]
  Q11 = Sharp PC817 [package=THT]
  Q12 = NPN-Transistor [part_number=2N2222A package="TO92 [THT]"]
  R34 = Resistor [tolerance=±5% resistance=1k package=THT]
  R35 = Resistor [tolerance=±5% resistance=1k package=THT]
  Q13 = Sharp PC817 [package=THT]
  Q14 = NPN-Transistor [part_number=2N2222A package="TO92 [THT]"]
  R36 = Resistor [tolerance=±5% resistance=1k package=THT]
  J78 = 3pth XH JST Custom [form="♀ (female rounded)" package=THT]
  J79 = rounded female pin header, 2 pins [form="♀ (female rounded)"]
  R37 = Resistor [tolerance=±5% resistance=1k package=THT]
  LED1 = LED - 3mm [color="Red (633nm)" package="3 mm [THT]"]
  D11 = Diode [package=diode-1n4148]
  RL3 = OMRON PCB Power Relay – G5LE [part_number="G5LE-1\n" package=THT]
  RL4 = OMRON PCB Power Relay – G5LE [part_number="G5LE-1\n" package=THT]
  D12 = Diode [package=diode-1n4148]
  R_B = screw terminal, 2 pins
  R38 = Resistor [tolerance=±5% resistance=150k package=THT]
  R_Y_B = screw terminal, 3 pins
  R39 = Resistor [tolerance=±5% resistance=150k package=THT]
  R40 = Resistor [tolerance=±5% resistance=15k package=THT]
  R41 = Resistor [tolerance=±5% resistance=68k package=THT]
  R42 = Resistor [tolerance=±5% resistance=150k package=THT]
  C14 = Capacitor [part_number=0.047uF package=cap-pth-large]
  R43 = Resistor [tolerance=±5% resistance=150k package=THT]
  C15 = Capacitor [part_number=0.047uF package=cap-pth-large]
  J84 = 3pth XH JST Custom [form="♀ (female rounded)" package=THT]
  Q17 = MOSFET-NCHANNEL [package=sot23-3]
  U9 = MOV [package=v18za2p]
  R48 = Resistor [tolerance=±5% resistance=22k package=THT]
  4V_Step_Down = MP1584 Step Down Module [part_number=MP1584]
  S3 = Push Button Switch [package=os]
  D7 = Diode [package=diode-1n4001]
  R49 = Resistor [tolerance=±5% resistance=500 package=THT]
  Q18 = Sharp PC817 [package=THT]
  C16 = Capacitor Polarized [package=cpol-radial-100uf-25v]
  C17 = Ceramic Capacitor [capacitance="100 nF" package="100 mil [THT, multilayer]"]
  C18 = Ceramic Capacitor [capacitance="100 nF" package="100 mil [THT, multilayer]"]
  R54 = Resistor [tolerance=±5% resistance=10k package=THT]
  R55 = Resistor [tolerance=±5% resistance=10k package=THT]
  R56 = Resistor [tolerance=±5% resistance=2.2k package=THT]
  R57 = Resistor [tolerance=±5% resistance=3.3k package=THT]
  M2 = LM339 [package="DIP (Dual Inline) [THT]"]
  D17 = Diode [part_number="2V7 Zener Diode" package=diode-1n4148]
  R58 = Resistor [tolerance=±5% resistance=2.2k package=THT]
  R59 = Resistor [tolerance=±5% resistance=10k package=THT]
  R60 = Resistor [tolerance=±5% resistance=10k package=THT]
  R61 = Resistor [tolerance=±5% resistance=1k package=THT]
  C19 = Electrolytic Capacitor [capacitance=33µF voltage=25V package="100 mil [THT, electrolytic]"]
  R63 = Resistor [tolerance=±5% resistance=10k package=THT]
  C21 = Ceramic Capacitor [capacitance="100 nF" package="100 mil [THT, multilayer]"]
  R64 = Resistor [tolerance=±5% resistance=0 package=THT]
  R66 = Resistor [tolerance=±5% resistance=3.3k package=THT]
  D9 = Diode [package=sma-diode]
  R67 = Resistor [tolerance=±5% resistance=0 package=THT]
  R68 = Resistor [tolerance=±5% resistance=10k package=THT]
  Q19 = NPN-Transistor [part_number=2N2222A package="TO92 [THT]"]
  R69 = Resistor [tolerance=±5% resistance=10k package=THT]
  RESET2 = Pushbutton [package="[THT]"]
  R70 = Resistor [tolerance=±5% resistance=0 package=THT]  # not connected
  S4 = Push Button Switch [package=os]
  S1_S2_N1_N2 = screw terminal, 4 pins
  Pad2 = Pad [width=3.9238365597985441 height=6.5558989380799284 connect=center]
  Pad3 = Pad [width=3.5191780907596595 height=16.22380405071431 connect=center]
  G2 = Graetz Bridge Rectifier [package="DIP (Dual Inline) [THT]"]
  J88 = 3pth XH JST Custom [form="♀ (female rounded)" package=THT]
  Pad4 = Pad [width=3.5456884675734743 height=14.083339303166316 connect=center]
  Pad5 = Pad [width=3.5456884675734743 height=14.083339303166316 connect=center]
  R71 = Resistor [tolerance=±5% resistance=10k package=THT]
  R72 = Resistor [tolerance=±5% resistance=10k package=THT]
  R73 = Resistor [tolerance=±5% resistance=10k package=THT]
  J89 = rounded female pin header, 2 pins [form="♀ (female rounded)"]
  J90 = rounded female pin header, 2 pins [form="♀ (female rounded)"]
  J91 = rounded female pin header, 2 pins [form="♀ (female rounded)"]
  J92 = rounded female pin header, 2 pins [form="♀ (female rounded)"]
  LM2596_Module2 = LM2596 Step Down Module
  J93 = rounded female pin header, 2 pins [form="♀ (female rounded)"]
  J58 = rounded female pin header, 4 pins [form="♀ (female rounded)"]
  U3 = atmega328 [package=dip]
  J94 = 3pth XH JST Custom [form="♀ (female rounded)" package=THT]
  J95 = 3pth XH JST Custom [form="♀ (female rounded)" package=THT]
  J81 = 4pth XH JST CUSTOM [form="♀ (female rounded)" package=THT]
  D18 = Diode [package=sma-diode]
  C22 = Electrolytic Capacitor [capacitance=33µF voltage=25V package="100 mil [THT, electrolytic]"]
  D19 = Diode [package=sma-diode]
  J60 = Rectifier_6A [package=THT]
  C23 = Electrolytic Capacitor [capacitance=0.47mF voltage=10V package="100 mil [THT, electrolytic]"]
  TP4056_Battery_Charge_Module4 = TP4056 Lithium Ion Battery Charger
  Fuse1 = Fuse with Handler  # not connected
  LM2596_Module3 = LM2596 Step Down Module  # not connected

nets:
  N1: R17.Pin_0, C7.1, C9.1, C8.1, SIM800L_20MM1.PIN2, C12.+, R32.Pin_1, Q17.D, R58.Pin_1, R59.Pin_1, R64.Pin_0, R66.Pin_1, J93.pin1, J93.pin2, U3.VCC, U3.AVCC, U3.AREF, C23.+
  N2: R17.Pin_1, RESET1.Pin_1, RESET1.Pin_2, U3.RESET
  N3: XTAL.pin_0, C5.0, U3.XLAT1
  N4: XTAL.pin_1, C6.1, U3.XLAT2
  N5: R15.Pin_0, Q2.B
  N6: R15.Pin_1, U3.D4
  N7: Q2.C, SIM800L_20MM1.PIN_8
  N8: C5.1, C7.0, U3.GND#7
  N9: -.pin1, TP4056_Battery_Charge_Module4.B+
  N10: -.pin2, S4.NO1, S4.NO2
  N11: C10.+, R14.Pin_1, C17.0, J94.pin3
  N12: R14.Pin_0, U3.D11_(PWM)
  N13: R16.Pin_0, SIM800L_20MM1.PIN_7
  N14: R16.Pin_1, U3.D2
  N15: C9.0, U3.GND#21
  N16: C8.0, SIM800L_20MM1.PIN_6
  N17: Q10.G, R54.Pin_0, R67.Pin_0
  N18: Q10.S, Q17.S, R54.Pin_1, D9.C, RESET2.Pin_3, RESET2.Pin_4, R73.Pin_1
  N19: Q10.D, J90.pin1, J90.pin2, TP4056_Battery_Charge_Module4.OUT+
  N20: R25.Pin_0, R_B.pin2
  N21: R25.Pin_1, R29.Pin_0, U9.P$2
  N22: R29.Pin_1, Q18.Pin_1
  N23: R24.Pin_0, R_B.pin1
  N24: R24.Pin_1, U9.P$1, D7.C
  N25: R28.Pin_0, Q18.Pin_2
  N26: R28.Pin_1, D7.A
  N27: SIM800L_20MM1.PIN_4, J79.pin2
  N28: SIM800L_20MM1.PIN_5, J79.pin1
  N29: J48.pin1, U3.D0_(RX)
  N30: J48.pin2, U3.D1_(TX)
  N31: RESET1.Pin_3, RESET1.Pin_4
  N32: J77.pin1, J60.AC_IN#2
  N33: J77.pin2, J60.AC_IN#1
  N34: R30.Pin_0, U3.D3_(PWM)
  N35: R30.Pin_1, 4V_Step_Down.OUT+, D9.A, R69.Pin_1, RESET2.Pin_1, R72.Pin_1
  N36: C2.+, D19.A, J60.DC_+
  N37: C2.-, S3.C1, J60.DC_-
  N38: R32.Pin_0, R33.Pin_0, M2.+_Input_2
  N39: Q11.Pin_1, Q13.Pin_1, R36.Pin_0
  N40: Q11.Pin_2, U3.A0
  N41: Q11.Pin_4, Q13.Pin_4, R36.Pin_1, J78.pin3, M2.Vcc, C21.1, R64.Pin_1, J81.pin4
  N42: Q11.Pin_3, R34.Pin_1
  N43: Q12.B, R34.Pin_0
  N44: Q12.C, J78.pin1
  N45: R35.Pin_0, Q13.Pin_3
  N46: R35.Pin_1, Q14.B
  N47: Q13.Pin_2, U3.D13
  N48: Q14.C, J78.pin2
  N49: R37.Pin_1, LED1.cathode
  N50: LED1.anode, U3.A5
  N51: D11.A, RL4.COIL1, J88.pin2
  N52: D11.C, RL3.COIL1, RL4.COIL2, D12.C, J88.pin3
  N53: RL3.A, S1_S2_N1_N2.pin4
  N54: RL3.C, RL4.C, S1_S2_N1_N2.pin1, S1_S2_N1_N2.pin3
  N55: RL3.COIL2, D12.A, J88.pin1
  N56: RL4.A, S1_S2_N1_N2.pin2
  N57: R38.Pin_0, R_Y_B.pin3, J84.pin1
  N58: R38.Pin_1, R42.Pin_1, Pad2.pad, Pad3.pad, G2.ac_input_1
  N59: R_Y_B.pin1, R41.Pin_1
  N60: R_Y_B.pin2, R42.Pin_0, C14.2, J84.pin3
  N61: R39.Pin_0, R40.Pin_0, Pad5.pad
  N62: R39.Pin_1, R43.Pin_0, C15.2
  N63: R40.Pin_1, R41.Pin_0, Pad4.pad
  N64: C14.1, C15.1
  N65: R43.Pin_1, G2.ac_input_2
  N66: Q17.G, Q19.C, R73.Pin_0
  N67: R48.Pin_0, Q18.Pin_3, C16.-, G2.dc_negative, J95.pin1
  N68: R48.Pin_1, C16.+, G2.dc_positive, J95.pin2
  N69: 4V_Step_Down.IN+, R55.Pin_0, R71.Pin_0, J91.pin1, J91.pin2, LM2596_Module2.IN+, D19.C
  N70: 4V_Step_Down.OUT-, R72.Pin_0
  N71: S3.C2, S4.C1, S4.C2, J89.pin1, J89.pin2
  N72: R49.Pin_0, C18.1, J94.pin2
  N73: R49.Pin_1, M2.-_Input_2
  N74: Q18.Pin_4, J95.pin3
  N75: C18.0, J94.pin1
  N76: R55.Pin_1, R57.Pin_1, M2.+_Input_3
  N77: R56.Pin_1, M2.-_Input_3, R66.Pin_0
  N78: R57.Pin_0, D17.A, R60.Pin_0
  N79: M2.Output_2, R61.Pin_1
  N80: M2.Output_1, R63.Pin_0
  N81: M2.-_Input_1, D17.C, R58.Pin_0
  N82: M2.+_Input_1, R59.Pin_0, R60.Pin_1
  N83: M2.Output_3, R67.Pin_1
  N84: R61.Pin_0, C19.+, U3.D10_(PWM)
  N85: C19.-, C22.-
  N86: R63.Pin_1, U3.D9_(PWM), C22.+
  N87: R68.Pin_0, J58.pin3, U3.D7
  N88: R68.Pin_1, Q19.B, R69.Pin_0
  N89: J92.pin1, J92.pin2, LM2596_Module2.OUT+, D18.A
  N90: J58.pin1, U3.D5_(PWM)
  N91: J58.pin2, U3.D6_(PWM)
  N92: J58.pin4, U3.D8
  N93: U3.A2, J81.pin1
  N94: U3.A3, J81.pin2
  N95: U3.A4, J81.pin3
  N96: D18.C, TP4056_Battery_Charge_Module4.IN+
  N97: TP4056_Battery_Charge_Module4.B-, TP4056_Battery_Charge_Module4.OUT-

notes:
  M-
  RX
  TX
  STX
  SRX
  1
  MOTOR
  FeedBack
  +
  Battery
  J1

custom parts:
  2PTH JST FROM HEADER 5: Generic rounded female header
  3pth XH JST Custom: 3PTH XH JST
  MOV: Metal Oxide Varistor
  MP1584 Step Down Module: Step Down Module based on MP1584
  Push Button Switch: DPDT On/Off Switch, when pressed connects NO to C.
  LM339: LM339 Quad Comparator IC. DIP14 Package.
  Graetz Bridge Rectifier: Graetz Bridge Rectifier - znany także jako Mostek Graetz'a :)
  LM2596 Step Down Module: LM2596 Step Down Regulator
  Rectifier_6A: stand Up rectifier 6A
  TP4056 Lithium Ion Battery Charger: A lithium battery charging and powering shield.
  Fuse with Handler: Device used to protect against excessive current.
